# Fritzing sketch MyRegenBox v5 (saved by Fritzing 1.0.0rc)
circuit board: 12cm x 6.7cm
breadboards: 2

parts:
  IC2 = 4060 [package="DIP16 [THT]"]
  R11 = Resistor [tolerance=±5% power=0.25W resistance=130k package=THT]
  R12 = Resistor [tolerance=±5% power=0.25W resistance=22k package=THT]
  D3 = Rectifier Diode [part_number=1N4001 package="300 mil [THT]"]
  D4 = Rectifier Diode [part_number=1N4001 package="300 mil [THT]"]
  D5 = Rectifier Diode [part_number=1N4001 package="300 mil [THT]"]
  IC1 = Voltage Regulator - Variable [part_number=LM317T package="TO220 [THT]"]
  R3 = Resistor [tolerance=±5% power=0.25W resistance=240 package=THT]
  R9 = Resistor [tolerance=±5% power=0.25W resistance=1k package=THT]
  R1 = Resistor [tolerance=±5% power=0.25W resistance=1k package=THT]
  R4 = Resistor [tolerance=±5% power=0.25W resistance=240 package=THT]
  P1 = 6mm Trimmer Potentiometer [maximum_resistance=100Ω knob_status=50% power=0.5W package=THT]
  BAT4 = Battery Holders [package=battery-aa-kit]
  BAT3 = Battery Holders [package=battery-aa-kit]
  BAT1 = Battery Holders [package=battery-aa-kit]
  BAT2 = Battery Holders [package=battery-aa-kit]
  D8 = Small signal Diode flat 300mil [part_number=1N4148 package="300 mil [THT]"]
  D2 = Rectifier Diode [part_number=1N4001 package="300 mil [THT]"]
  R8 = Resistor [tolerance=±5% power=0.25W resistance=1k package=THT]
  TP4 = Header 1 [package=1x01_offset]
  TP3 = Header 1 [package=1x01_offset]
  C3 = Electrolytic Capacitor [capacitance=220µ voltage=16V package="200 mil [THT, electrolytic]"]
  R6 = Resistor [tolerance=±5% power=1W resistance=3.3 package=THT]
  T2 = NPN-Transistor [part_number=BC337 package="TO92 [THT]"]
  T1 = NPN-Transistor [part_number=BC337 package="TO92 [THT]"]
  TP1 = Header 1 [package=1x01_offset]
  TP5 = Header 1 [package=1x01_offset]
  TP2 = Header 1 [package=1x01_offset]
  R5 = Resistor [tolerance=±5% power=0.25W resistance=10k package=THT]
  R2 = Resistor [tolerance=±5% power=0.25W resistance=10k package=THT]
  LED1 = LED - 3mm [color="Red (633nm)" current=0.030A package="3 mm [THT]"]
  LED3 = LED - 3mm [color="Green (565nm)" current=0.030A package="3 mm [THT]"]
  LED2 = LED - 3mm [color="Yellow (592nm)" current=0.030A package="3 mm [THT]"]
  R7 = Resistor [tolerance=±5% power=0.25W resistance=1k package=THT]
  D6 = Schottky Diode [part_number=BAT41 package="300 mil [THT]"]
  T3 = BF245 JFET N-Channel [part_number=BF245 package=TO92]
  S1 = Toggle Switch spst [package=THT]
  J2 = Power Jack [package=power_jack_pth]
  F1 = FUSE [part_number="500 mA" package=fuse_5mm]
  VM1 = Voltmeter (3 wire)
  C1 = Ceramic Capacitor top view [capacitance="100 nF" voltage=35V package="200 mil"]
  C2 = Ceramic Capacitor top view [capacitance="100 nF" voltage=35V package="200 mil"]
  C4 = Ceramic Capacitor [capacitance=150nF voltage=35V package="200 mil [THT, multilayer]"]
  D10 = Rectifier Diode [part_number=1N4001 package="300 mil [THT]"]
  D1 = Rectifier Diode [part_number=1N4001 package="300 mil [THT]"]
  R10 = Resistor [tolerance=±5% power=0.25W resistance=4.7k package=THT]
  D9 = Small signal Diode flat 300mil [part_number=1N4148 package="300 mil [THT]"]
  D7 = Small signal Diode flat 300mil [part_number=1N4148 package="300 mil [THT]"]

nets:
  N1: IC2.Q12, D7.anode
  N2: IC2.Q13, R9.Pin_1, D8.anode
  N3: IC2.Q6, D9.anode
  GND: IC2.GND, R3.Pin_0, R8.Pin_0, TP3.1, C3.-, R6.Pin_0, T2.E, T1.E, LED1.cathode, LED3.cathode, D6.cathode, S1.L1, VM1.GND, C2.0, D10.anode
  ≈2,1 kHz: IC2.CEXT, TP5.1, C4.1
  N4: IC2.REXT, R12.Pin_0
  N5: IC2.RS, R11.Pin_0
  N6: IC2.MR, R8.Pin_1, TP4.1, C1.1
  5...15V (5V javasolt): IC2.VDD, IC1.IN, C3.+, R7.Pin_1, F1.2, VM1.VCC, C1.0, C2.1, D10.cathode, D1.cathode
  N7: R11.Pin_1, R12.Pin_1, C4.0
  N8: D3.cathode, BAT2.+
  ≈2,45 V: D3.anode, D4.anode, D5.anode, IC1.OUT, R1.Pin_0, R4.Pin_0, D2.anode, TP1.1, D1.anode
  N9: D4.cathode, BAT3.+
  N10: D5.cathode, BAT4.+
  N11: IC1.ADJ, P1.wiper, T2.C, T1.C, TP2.1
  N12: R3.Pin_1, P1.leg1
  N13: R9.Pin_0, LED3.anode
  N14: R1.Pin_1, LED1.anode
  N15: R4.Pin_1, P1.leg2
  N16: BAT4.-, BAT3.-, BAT1.-, BAT2.-, R6.Pin_1, R5.Pin_0, R2.Pin_0
  ≈1,75V: BAT1.+, D2.cathode, VM1.Vin
  ≈0,5÷1,5 s: D8.cathode, R10.Pin_1, D9.cathode, D7.cathode
  N17: T2.B, R10.Pin_0
  N18: T1.B, R5.Pin_1
  N19: R2.Pin_1, T3.gate
  N20: LED2.cathode, T3.drain
  N21: LED2.anode, R7.Pin_0
  N22: D6.anode, T3.source
  N23: S1.COM, J2.GND, J2.GNDBREAK
  N24: J2.PWR, F1.1

notes:
  CLOCK
  REGEN
  CURRENT

custom parts:
  Small signal Diode flat 300mil: Small signal diode such as the 1n4148 Footprint: mounted flat on 300mil centers.
  BF245 JFET N-Channel: A BF245 JFET N-Channel Transistor
  Toggle Switch spst: Toggle Switch single pole single throw
  Voltmeter (3 wire): Voltmeter, 3 digit LED (.56 inch) output, 3 wire (Power 3.5V to 30V, Ground, Vin) comes in several colors (red, green, orange, blue). Available from Ebay and Amazon and others, no bezel (although bezels to fit them are currently available on Ebay). The mounting ears on what you get may or may not be the same as the ones I have. Won't run on 3.3V so you would need a 5 volt source or a 3V to 5V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
  Ceramic Capacitor top view: 100 nF multilayer Ceramic Capacitor breadboard set to top view for perfboard use.
